# Fritzing sketch belepteto (saved by Fritzing 0.9.10b)
circuit board: 8.46667cm x 5.64444cm

parts:
  Keypad4x1 = Keypad Membran 4x4
  Part2 = LCD1602-I2C
  J1 = Piezo Speaker
  Ardunino = Arduino Nano (Rev3.0)
  Logikai_szintillesztő_(Ez_majd_IC_formájában_lesz_a_penelen) = Logic Level Converter
  Mifare_olvasó = RFID-RC522-v2

nets:
  N1: Keypad4x1.Pin1, Ardunino.D9
  N2: Keypad4x1.Pin2, Ardunino.D8
  N3: Keypad4x1.Pin3, Ardunino.D7
  N4: Keypad4x1.Pin4, Ardunino.D6
  N5: Keypad4x1.Pin5, Ardunino.D5
  N6: Keypad4x1.Pin6, Ardunino.D4
  N7: Keypad4x1.Pin7, Ardunino.D3
  N8: Keypad4x1.Pin8, Ardunino.D2
  GND: Part2.GND, J1.pin1, Ardunino.GND, Logikai_szintillesztő_(Ez_majd_IC_formájában_lesz_a_penelen).GND
  VCC: Part2.VCC, Ardunino.5V, Logikai_szintillesztő_(Ez_majd_IC_formájában_lesz_a_penelen).HV
  N9: Part2.SDA, Ardunino.A4
  N10: Part2.SCL, Ardunino.A5
  N11: J1.pin2, Ardunino.A0
  N12: Ardunino.D1/TX, Logikai_szintillesztő_(Ez_majd_IC_formájában_lesz_a_penelen).TX2_LV
  N13: Ardunino.D0/RX, Logikai_szintillesztő_(Ez_majd_IC_formájában_lesz_a_penelen).RX2_LV
  N14: Ardunino.D10, Mifare_olvasó.SDA
  N15: Ardunino.D11/MOSI, Mifare_olvasó.MOSI
  N16: Ardunino.D12/MISO, Mifare_olvasó.MISO
  3V3: Ardunino.3V3, Mifare_olvasó.3.3V
  N17: Ardunino.D13/SCK, Mifare_olvasó.SCK

custom parts:
  Keypad Membran 4x4: Membrane Keypad 4x4 Matrix
  LCD1602-I2C: A standard character display, usually with 2x16 characters. Comes in many colors with LCM1602 IIC attached.
  RFID-RC522-v2: A simple China made RFID-RC522 Reader; do check the pin labels, as this is a MFRC522 based clone.
