# Fritzing sketch belepteto_rpi (saved by Fritzing 0.9.10b)
breadboards: 1

parts:
  SG1 = Buzzer 12mm [package=buzzer-12mm-ns]
  Part1 = RFID-RC522-v2
  Raspberry_Pi1 = Raspberry Pi B rev2

nets:
  GND: SG1.1, Part1.GND, Raspberry_Pi1.GND
  N1: SG1.2, Raspberry_Pi1.GPIO_4
  N2: Part1.SDA, Raspberry_Pi1.GPIO_8
  N3: Part1.SCK, Raspberry_Pi1.GPIO_11
  N4: Part1.MOSI, Raspberry_Pi1.GPIO_10
  N5: Part1.MISO, Raspberry_Pi1.GPIO_9
  N6: Part1.RST, Raspberry_Pi1.GPIO_25
  3.3V: Part1.3.3V, Raspberry_Pi1.3V3

custom parts:
  RFID-RC522-v2: A simple China made RFID-RC522 Reader; do check the pin labels, as this is a MFRC522 based clone.
